# Fritzing sketch ChopperControl (saved by Fritzing 0.3.16b)

parts:
  Arduino1 = Arduino
  J2 = Basic Servo
  J3 = Basic Servo
  M1 = DC Motor
  M2 = DC Motor
  J4 = Infrared Proximity Sensor
  Q1 = Basic FET N-Channel [package="TO220 [THT]"]
  Q2 = Basic FET N-Channel [package="TO220 [THT]"]
  J5 = Basic Servo
  VCC1 = obsolete Battery
  R1 = Resistor [resistance=4.7k package=THT]
  R1_2 = Resistor [resistance=4.7k package=THT]
  U1 = Voltage Regulator - Variable [package="TO220 [THT]"]
  D1 = Rectifier Diode [package="300 mil [THT]"]
  C1 = Electrolytic Capacitor [package=THT]
  R2 = Resistor [resistance=10k package=THT]
  R3 = Trimmer Potentiometer [package=THT]
  U3 = mystery part, 4 pins [chip_label=Compass spacing=300mil]  # not connected
  D2 = Rectifier Diode [package="300 mil [THT]"]
  D3 = Rectifier Diode [package="300 mil [THT]"]
  C2 = Electrolytic Capacitor [package=THT]
  C3 = Electrolytic Capacitor [package=THT]
  C3_2 = Electrolytic Capacitor [package=THT]
  J6 = Infrared Proximity Sensor
  U4 = mystery part, 4 pins [chip_label="Intersema MS5534B Baro" spacing=300mil]

nets:
  GND: Arduino1.GND, J2.gnd, J3.gnd, J4.GND, Q1.source, Q2.source, J5.gnd, VCC1.-, R1.Pin_0, R1_2.Pin_1, C1.-, R3.leg2, C2.-, J6.GND
  N1: Arduino1.D13, J3.pulse
  N2: Arduino1.D12, J2.pulse
  N3: Arduino1.D10, J5.pulse
  N4: Arduino1.D6, Q1.gate, R1.Pin_1
  N5: Arduino1.D5, Q2.gate, R1_2.Pin_0
  N6: Arduino1.D2, D3.anode
  VCC: Arduino1.+5V, J4.Vcc, J5.vcc, J6.Vcc
  N7: Arduino1.VIN, U1.OUT, D1.anode, C1.+, R2.Pin_0
  N8: Arduino1.A2, J6.Vout
  N9: Arduino1.A3, J4.Vout
  VCC_2: J2.vcc, J3.vcc, M1.pin_2, M2.pin_2, VCC1.+, U1.IN, D1.cathode, C2.+, C3.+, C3_2.+
  N10: M1.pin_1, Q2.drain, C3.-
  N11: M2.pin_1, Q1.drain, C3_2.-
  N12: U1.ADJ, R2.Pin_1, R3.wiper
  N13: D2.cathode, U4.pin1
  N14: D2.anode, D3.cathode
